# Fritzing sketch Bela (saved by Fritzing 0.9.3b)

parts:
  GY1 = MPU-6050 Board GY-521 [form="♀ (female)" package=THT]
  Bauteil2 = 16-Channel 12-bit PWM Servo Driver - I2C [part_number=815]
  Raspberry_Pi_1 = Raspberry Pi 3 [part_number=RPI-3-V1.2]
  IR = TSOP312.., 314.. [package=THT]
  Buzzer = Piezo Speaker
  Microphone = MIC [package=mic-9.7mm]  # not connected
  U2 = SWITCH_SPDT [package=kps-1290]
  MG92b_x_12 = Basic Servo
  Bauteil3 = Arduino Pro Mini v13
  10V_1500_uF = Capacitor Polarized [package=panasonic_e]
  Speaker = SPEAKER [package=pcb_mount_speaker]  # not connected
  EEPROM = 24LC256 [package=THT]
  6_66_V_/_5A_max = RioRand LM2596
  BT1 = Bluetooth HC-06u [package=THT]
  LED1 = 7-SEGMENT-4DIGIT-YOUNGSUN [package=7-segment-4digit-youngsun]  # not connected
  U3 = 7-SEGMENT-4DIGIT [package=7-segment-4digit-youngsun]  # not connected
  5_V = Graphical LCD 128x64 [package=1x20]
  - = Graphical LCD 128x64 [package=1x20]
  5_V_2 = RioRand LM2596
  3_3_V_to_5_V_Shifter = I2C level shifter bidirectional

nets:
  N1: GY1.pin1, Bauteil2.VCC, 5_V.CS2
  N2: GY1.pin2, Bauteil2.GND, 10V_1500_uF.-, -.DB4
  N3: GY1.pin3, Bauteil2.SCL, Bauteil3.A5, EEPROM.SCL_-_I2C_Clock
  N4: GY1.pin4, Bauteil2.SDA, Bauteil3.A4
  N5: GY1.pin8, Bauteil3.D2
  N6: Bauteil2.5.0V, 10V_1500_uF.+
  N7: Bauteil2.PWM15, MG92b_x_12.pulse
  N8: Raspberry_Pi_1.3v3, 3_3_V_to_5_V_Shifter.LV
  N9: Raspberry_Pi_1.GIPO15, 3_3_V_to_5_V_Shifter.LV4
  N10: Raspberry_Pi_1.GIPO14, 3_3_V_to_5_V_Shifter.LV3
  N11: Raspberry_Pi_1.GND, 5_V_2.Pin_4
  N12: Raspberry_Pi_1.5V, 5_V_2.Pin_3
  GND: IR.GND, MG92b_x_12.gnd, -.K
  N13: IR.Vs, 5_V.K
  N14: IR.Data, Bauteil3.D4
  N15: Buzzer.pin1, Bauteil3.GND
  N16: Buzzer.pin2, Bauteil3.D5_PWM
  N17: U2.P, 6_66_V_/_5A_max.Pin_3
  N18: U2.S, Bauteil3.RAW
  N19: Bauteil3.VCC, 5_V.CS1
  N20: Bauteil3.D1/RX, 3_3_V_to_5_V_Shifter.HV4
  N21: Bauteil3.D0/TX, 3_3_V_to_5_V_Shifter.HV3
  N22: 6_66_V_/_5A_max.Pin_4, -.VDD
  N23: BT1.VCC, 5_V.DB7
  N24: BT1.GND, -.CS2
  N25: 5_V.E, 3_3_V_to_5_V_Shifter.HV
  N26: -.VSS, -.DB0
  N27: -.R_W, -.A, 3_3_V_to_5_V_Shifter.GND

notes:
  Lipo 7.2 V 2200mAh

custom parts:
  MPU-6050 Board GY-521: Acelerometro y Giroscopio MPU-6050 Board GY-521
  16-Channel 12-bit PWM Servo Driver - I2C: You want to make a cool robot, maybe a hexapod walker, or maybe just a piece of art with a lot of moving parts. Or maybe you want to drive a lot of LEDs with precise PWM output. Using only two pins, control 16 free-running PWM outputs! You can even chain up 62 breakouts to control up to 992 PWM outputs.
  Bluetooth HC-06u: Bluetooth HC-06 - face up, pins down 16.5mm x 37.5mm PCB
