# Fritzing sketch Bela_HV_servos (saved by Fritzing 0.9.3b)

parts:
  GY1 = MPU-6050 Board GY-521 [form="♀ (female)" package=THT]
  Bauteil2 = 16-Channel 12-bit PWM Servo Driver - I2C [part_number=815]
  Raspberry_Pi_1 = Raspberry Pi 3 [part_number=RPI-3-V1.2]
  IR = TSOP312.., 314.. [package=THT]
  Buzzer = Piezo Speaker
  Bauteil3 = Arduino Pro Mini v13
  10V_1500_uF = Capacitor Polarized [package=panasonic_e]
  EEPROM = 24LC256 [package=THT]
  BT1 = Bluetooth HC-06u [package=THT]
  5_V = Graphical LCD 128x64 [package=1x20]
  5_V_2 = RioRand LM2596
  3_3_V_to_5_V_Shifter = I2C level shifter bidirectional
  R1 = Resistor [package="2010 [SMD]"]
  U2 = SWITCH_SPDT [package=kps-1290]
  - = Graphical LCD 128x64 [package=1x20]
  J1 = Basic Servo

nets:
  N1: GY1.pin1, Bauteil2.VCC, 5_V.CS2, R1.Pin_0
  GND: GY1.pin2, Bauteil2.GND, 10V_1500_uF.-, -.DB4, J1.gnd
  N2: GY1.pin3, Bauteil2.SCL, Bauteil3.A5, EEPROM.SCL_-_I2C_Clock
  N3: GY1.pin4, Bauteil2.SDA
  N4: GY1.pin8, Bauteil3.D2
  N5: Bauteil2.5.0V, 10V_1500_uF.+, J1.vcc
  N6: Bauteil2.PWRIN, U2.S
  N7: Bauteil2.PWM15, J1.pulse
  N8: Raspberry_Pi_1.3v3, 3_3_V_to_5_V_Shifter.LV
  N9: Raspberry_Pi_1.GIPO15, 3_3_V_to_5_V_Shifter.LV4
  N10: Raspberry_Pi_1.GIPO14, 3_3_V_to_5_V_Shifter.LV3
  N11: Raspberry_Pi_1.GND, 5_V_2.Pin_4
  N12: Raspberry_Pi_1.5V, 5_V_2.Pin_3
  N13: IR.GND, -.K
  N14: IR.Vs, 5_V.K
  N15: IR.Data, Bauteil3.D4
  N16: Buzzer.pin1, Bauteil3.GND, -.RST
  N17: Buzzer.pin2, Bauteil3.D5_PWM
  N18: Bauteil3.VCC, 5_V.CS1
  N19: Bauteil3.D1/RX, 3_3_V_to_5_V_Shifter.HV3
  N20: Bauteil3.D0/TX, 3_3_V_to_5_V_Shifter.HV4
  N21: EEPROM.SDA_-_I2C_Data, R1.Pin_1
  N22: BT1.VCC, 5_V.DB0
  N23: BT1.GND, -.DB1
  N24: 5_V.E, 3_3_V_to_5_V_Shifter.HV
  N25: 3_3_V_to_5_V_Shifter.GND, -.R_W, -.A
  N26: -.VSS, -.DB0

notes:
  Lipo 7.2 V
  BEC 5V, 3A
  Front view
  | | |
  S G V
  idxpin
  13
  3
  14
  12
  9
  2
  10
  13
  5
  9
  6
  14
  Head
  10 Neck
  07
  28
  Tail
  4
  6
  7
  15
  8
  5
  11
  10
  12
  4
  15
  11
  2 x PCA9685 parallel
  to distribute the high current the 12 servos draw.

custom parts:
  MPU-6050 Board GY-521: Acelerometro y Giroscopio MPU-6050 Board GY-521
  16-Channel 12-bit PWM Servo Driver - I2C: You want to make a cool robot, maybe a hexapod walker, or maybe just a piece of art with a lot of moving parts. Or maybe you want to drive a lot of LEDs with precise PWM output. Using only two pins, control 16 free-running PWM outputs! You can even chain up 62 breakouts to control up to 992 PWM outputs.
  Bluetooth HC-06u: Bluetooth HC-06 - face up, pins down 16.5mm x 37.5mm PCB
  Resistor: Resistor Basic schematic elements and footprints for 0603, 1206, and PTH resistors.
