# Fritzing sketch Bela (saved by Fritzing 0.9.3b)

parts:
  GY1 = MPU-6050 Board GY-521 [form="♀ (female)" package=THT]
  Bauteil2 = 16-Channel 12-bit PWM Servo Driver - I2C [part_number=815]
  Raspberry_Pi_1 = Raspberry Pi 3 [part_number=RPI-3-V1.2]
  IR1 = TSOP312.., 314.. [package=THT]
  Buzzer = Piezo Speaker
  Microphone = MIC [package=mic-9.7mm]  # not connected
  U2 = SWITCH_SPDT [package=kps-1290]
  MG996R_x_8 = Basic Servo
  Bauteil3 = Arduino Pro Mini v13
  10V_1500_uF = Capacitor Polarized [package=panasonic_e]
  Speaker = SPEAKER [package=pcb_mount_speaker]  # not connected
  EEPROM = 24LC256 [package=THT]

nets:
  N1: GY1.pin1, Bauteil2.VCC
  N2: GY1.pin2, GY1.pin3, Bauteil2.GND, Bauteil2.SCL, Bauteil2.OE, Bauteil3.A5, 10V_1500_uF.-, EEPROM.SCL_-_I2C_Clock
  N3: GY1.pin4, Bauteil2.SDA, Bauteil3.A4
  N4: GY1.pin8, Bauteil3.D2
  N5: Bauteil2.5.0V, U2.S, 10V_1500_uF.+
  N6: Bauteil2.PWM15, MG996R_x_8.pulse
  N7: Raspberry_Pi_1.GIPO14, Bauteil3.D1/RX
  N8: IR1.Data, Bauteil3.D4
  N9: Buzzer.pin1, Bauteil3.GND
  N10: Buzzer.pin2, Bauteil3.D5_PWM

notes:
  Lipo 7.2 V 2200mAh

custom parts:
  MPU-6050 Board GY-521: Acelerometro y Giroscopio MPU-6050 Board GY-521
  16-Channel 12-bit PWM Servo Driver - I2C: You want to make a cool robot, maybe a hexapod walker, or maybe just a piece of art with a lot of moving parts. Or maybe you want to drive a lot of LEDs with precise PWM output. Using only two pins, control 16 free-running PWM outputs! You can even chain up 62 breakouts to control up to 992 PWM outputs.
